# Fritzing sketch Devre şeması (saved by Fritzing 1.0.4)
breadboards: 1

parts:
  Mod1 = Amica NodeMCU DEVKIT 1.0
  LCD1 = LCD screen
  LCM1602_IIC1 = LCM1602 IIC [part_number="LCM1602 IIC" chip_label="LCM1602 IIC" package="DIP (Dual Inline) [THT]"]
  부품3 = FC-28 Soil Hygrometer Module - Probe
  부품4 = FC-28 Soil Hygrometer Module
  KY-2 = Keyes Relay [package=THT]
  WATER_PUMP1 = water pump/motor
  VCC1 = Battery block 9V [internal_resistance=0.1Ω]

nets:
  N1: Mod1.pin1, Mod1.pin_10, Mod1.pin_26, KY-2.signal
  GND: Mod1.pin2, Mod1.pin_9, Mod1.pin_25, Mod1.pin_29, LCM1602_IIC1.GND, 부품4.GND, KY-2.power
  N2: Mod1.pin_12, KY-2.ground
  N3: Mod1.pin_13, LCM1602_IIC1.SDA
  N4: Mod1.pin_14, LCM1602_IIC1.SCL
  N5: Mod1.pin_16, 부품4.AO
  VCC: Mod1.pin_30, LCM1602_IIC1.VCC, 부품4.VCC
  VSS: LCD1.VSS, LCM1602_IIC1.VSS
  VDD: LCD1.VDD, LCM1602_IIC1.VDD
  N6: LCD1.V0, LCM1602_IIC1.V0
  N7: LCD1.RS, LCM1602_IIC1.RS
  N8: LCD1.R/W, LCM1602_IIC1.RW
  N9: LCD1.E, LCM1602_IIC1.E
  N10: LCD1.DB0, LCM1602_IIC1.D0
  N11: LCD1.DB1, LCM1602_IIC1.D1
  N12: LCD1.DB2, LCM1602_IIC1.D2
  N13: LCD1.DB3, LCM1602_IIC1.D3
  N14: LCD1.DB4, LCM1602_IIC1.D4
  N15: LCD1.DB5, LCM1602_IIC1.D5
  N16: LCD1.DB6, LCM1602_IIC1.D6
  N17: LCD1.DB7, LCM1602_IIC1.D7
  N18: LCD1.LED+, LCM1602_IIC1.A
  N19: LCD1.LED-, LCM1602_IIC1.K
  N20: 부품3.POS, 부품4.POS
  N21: 부품3.NEG, 부품4.NEG
  N22: KY-2.C, VCC1.+
  N23: KY-2.NO, WATER_PUMP1.pin_2
  N24: WATER_PUMP1.pin_1, VCC1.-

notes:
  vcc(red)
  gnd(blue)
  ın(cyan)
  Abdulsamed Kurubal
  Osman yıldız

custom parts:
  LCM1602 IIC: I2C-Module to use a 1602 or 2004 LCD on with the wire.h libory Serial LCD Modul
  FC-28 Soil Hygrometer Module - Probe: The FC-28 is a soil hygrometer module that uses the Texas Instruments LM393 comparator chip to provide an analog measurement of soil humidity.
  FC-28 Soil Hygrometer Module: The FC-28 is a soil hygrometer module that uses the Texas Instruments LM393 comparator chip to provide an analog measurement of soil humidity. The digital output is high when soil moisture is over a certain threshold, as determined by adjusting the potentiometer.
  Keyes Relay: The Keyes 5V relay module is suitable for SCM development, home appliance control. It uses a 5V~12V TIL control signal which can control DC / AC signal.
  water pump/motor: WATER PUMP BY ARDUBLOCKTR
